// Logisim project GivenCache.circ as structural Verilog: 13 circuits, main circuit main
module main (
  input  EnableTestHalting,
  output [9:0] CorrectCounter,
  output [9:0] HitCounter,
  output [9:0] MissCounter,
  output [9:0] TestNumber,
  output [7:0] ByteRead,
  output [7:0] CorrectByteRead,
  output Halt
);

  wire and_3_out, and_4_out, and_5_out, CLK, CmdIsRead, Correct, CpuRead, CpuWrite, DidContain, HaltTesting,
       MaxItersReached, MemRead, MemWrite, not_1_out, not_2_out, not_4_out, NotDoneTesting, Ok2Count,
       or_1_out, Ready;
  wire [7:0] CpuWriteValue, MemAddress;
  wire [9:0] CpuAddress;
  wire [31:0] Line2Mem, LineFromMem;

  not not_1 (not_1_out, Ready);
  Clock clock_1 (.out(CLK));
  or or_1 (or_1_out, MaxItersReached, Ready);
  Counter #(.width(4), .max('h9)) MaxClocks (
    .load(Ready), .D(4'b0001), .count(not_1_out), .carry(MaxItersReached), .clk(CLK));  // open: Q, clr
  and and_1 (HaltTesting, EnableTestHalting, CmdIsRead, not_2_out);
  not not_2 (not_2_out, Correct);
  not not_3 (NotDoneTesting, Halt);
  Inputs inputs_1 (
    .HaltTesting(HaltTesting), .Ready(or_1_out), .CLK(CLK), .Done(Halt), .Read(CpuRead), .Write(CpuWrite),
    .Address(CpuAddress), .Value(CpuWriteValue), .TestNumber(TestNumber));
  Cache cache_1 (
    .CpuAddress(CpuAddress), .CpuRead(CpuRead), .CpuWrite(CpuWrite), .CpuWriteValue(CpuWriteValue),
    .CLK(CLK), .Ready(Ready), .DidContain(DidContain), .ByteRead(ByteRead), .MemAddress(MemAddress),
    .MemRead(MemRead), .MemWrite(MemWrite), .LineFromMem(LineFromMem), .Line2Mem(Line2Mem));
  // Probe on CpuRead
  // Probe on CpuWrite
  // Probe on CpuAddress
  // Probe on CpuWriteValue
  // Probe on TestNumber
  // Probe on CorrectByteRead
  // Probe on Correct
  // Probe on Ready
  // Probe on DidContain
  // Probe on ByteRead
  // Probe on MemAddress
  // Probe on MemRead
  // Probe on MemWrite
  // Probe on HitCounter
  // Probe on LineFromMem
  // Probe on Line2Mem
  not not_4 (not_4_out, HaltTesting);
  RAM #(.dataWidth(32), .bus("separate")) ram_1 (
    .addr(MemAddress), .din(Line2Mem), .data(LineFromMem), .str(MemWrite), .clk(CLK), .ld(MemRead));  // open: sel, clr
  and and_2 (Ok2Count, Ready, not_4_out, NotDoneTesting);
  and and_3 (and_3_out, Correct, Ok2Count);
  and and_4 (and_4_out, DidContain, Ok2Count);
  and and_5 (and_5_out, MemRead, NotDoneTesting);
  Checker checker_1 (
    .TestNumber(TestNumber), .YourByteRead(ByteRead), .CmdIsRead(CmdIsRead),
    .CorrectByteRead(CorrectByteRead), .Correct(Correct));
  Counter #(.width(10), .max('h3ff)) u_CorrectCounter (
    .count(and_3_out), .Q(CorrectCounter), .clk(CLK));  // open: load, D, carry, clr
  Counter #(.width(10), .max('h3ff)) u_HitCounter (
    .count(and_4_out), .Q(HitCounter), .clk(CLK));  // open: load, D, carry, clr
  Counter #(.width(10), .max('h3ff)) u_MissCounter (
    .count(and_5_out), .Q(MissCounter), .clk(CLK));  // open: load, D, carry, clr
  // Probe on CorrectCounter
  // Probe on HitCounter
  // Probe on MissCounter

  // Other names for the same wires on the sheet: DoneTesting = Halt

  // Notes on the sheet:
  //   Name: Fareeha Ahmed, ID: 999307283
  //   Partner's Name: Chetan Malhotra, ID: 997532445
endmodule

module Cache (
  input  [9:0] CpuAddress,
  input  CpuRead,
  input  CpuWrite,
  input  [7:0] CpuWriteValue,
  input  CLK,
  input  [31:0] LineFromMem,
  output Ready,
  output DidContain,
  output [7:0] ByteRead,
  output [7:0] MemAddress,
  output MemRead,
  output MemWrite,
  output [31:0] Line2Mem
);

  wire AgeStart, and_1_out, comparator_1_eq, Contains0, Contains1, CpuRead_t, CpuWrite_t, CurrContain, Dirty,
       Dirty0, Dirty1, NextAgeStart, NextLine, not_1_out, Write2Cache;
  wire [1:0] Offset;
  wire [2:0] state;
  wire [6:0] MTE, Tag, TE0, TE1;
  wire [7:0] Byte0, Byte1, CpuWriteValue_t;
  wire [31:0] LE0, LE1;

  not not_1 (not_1_out, MemAddress[0]);
  Register #(.width(20)) SaveVals (
    .D({CpuWriteValue, CpuWrite, CpuRead, CpuAddress}), .en(Ready),
    .Q({CpuWriteValue_t, CpuWrite_t, CpuRead_t, Tag, MemAddress[0], Offset}), .clk(CLK));  // open: clr
  Set Set0 (
    .CLK(CLK), .Tag(Tag), .Offset(Offset), .Write2Cache(Write2Cache), .Set(not_1_out), .AgeStart(AgeStart),
    .NextAgeStart(NextAgeStart), .CpuWriteValue(CpuWriteValue_t), .LineFromMem(LineFromMem),
    .NextLine(NextLine), .ByteRead(Byte0), .DidContain(Contains0), .Evict(Dirty0), .TagOfEvictedLine(TE0),
    .LineToWriteBack(LE0));
  Set Set1 (
    .CLK(CLK), .Tag(Tag), .Offset(Offset), .Write2Cache(Write2Cache), .Set(MemAddress[0]),
    .AgeStart(AgeStart), .NextAgeStart(NextAgeStart), .CpuWriteValue(CpuWriteValue_t),
    .LineFromMem(LineFromMem), .NextLine(NextLine), .ByteRead(Byte1), .DidContain(Contains1), .Evict(Dirty1),
    .TagOfEvictedLine(TE1), .LineToWriteBack(LE1));
  Multiplexer #(.width(8), .enable("false")) multiplexer_1 (
    .in0(Byte0), .in1(Byte1), .out(ByteRead), .sel(MemAddress[0]));
  Multiplexer #(.enable("false")) multiplexer_2 (.in0(Dirty0), .in1(Dirty1), .out(Dirty), .sel(MemAddress[0]));
  Multiplexer #(.width(7), .enable("false")) multiplexer_3 (.in0(TE0), .in1(TE1), .out(MTE), .sel(MemAddress[0]));
  Multiplexer #(.width(32), .enable("false")) multiplexer_4 (.in0(LE0), .in1(LE1), .out(Line2Mem), .sel(MemAddress[0]));
  Control control_1 (
    .CurrContain(CurrContain), .Dirty(Dirty), .CpuRead(CpuRead_t), .CpuWrite(CpuWrite_t), .CLK(CLK),
    .Ready(Ready), .AgesStart(AgeStart), .NextAgeStart(NextAgeStart), .Write2Cache(Write2Cache),
    .MemRead(MemRead), .NextLine(NextLine), .MemWrite(MemWrite), .state(state));
  and and_1 (and_1_out, MemWrite, Dirty);
  Multiplexer #(.width(7), .enable("false")) multiplexer_5 (
    .in0(Tag), .in1(MTE), .out(MemAddress[7:1]), .sel(and_1_out));
  Multiplexer #(.enable("false")) multiplexer_6 (
    .in0(Contains0), .in1(Contains1), .out(CurrContain), .sel(MemAddress[0]));
  Comparator #(.width(3), .mode("unsigned")) comparator_1 (
    .a(state), .b(3'b010), .eq(comparator_1_eq));  // open: gt, lt
  Register #(.width(1)) ContainsReg (.D(CurrContain), .en(comparator_1_eq), .Q(DidContain), .clk(CLK));  // open: clr

  // Other names for the same wires on the sheet: Set = MemAddress[0]

  // Notes on the sheet:
  //   Address Bits = 10
  //   W = 3
  //   Line Size = 4
  //   Num Sets = 2
  //   C =4*3*2 = 24bytes
endmodule

module Inputs (
  input  HaltTesting,
  input  Ready,
  input  CLK,
  output Done,
  output Read,
  output Write,
  output [9:0] Address,
  output [7:0] Value,
  output [9:0] TestNumber
);

  wire and_1_out, not_1_out, not_2_out;

  not not_1 (not_1_out, HaltTesting);
  not not_2 (not_2_out, Done);
  Counter #(.width(10), .max('h3ff), .ongoal("stay")) u_TestNumber (
    .count(and_1_out), .Q(TestNumber), .clk(CLK));  // open: load, D, carry, clr
  and and_1 (and_1_out, not_1_out, Ready, not_2_out);
  ROM #(.addrWidth(10), .dataWidth(21)) rom_1 (
    .addr(TestNumber), .data({Done, Read, Write, Address, Value}));  // open: sel

  // Notes on the sheet:
  //   contents of rom_1 (hex, n*v repeats v):
  //   80882 83fe6 4306b 83e0e 43701 42275 8280f 80304 41bd8 84371 43f77 41d70 4250b 44733 8253d 440d8
  //   82691 440c9 83d7c 43558 446bf 83837 842c9 43e0f 4059d 41556 80166 833b0 43a89 83142 8361c 42e66
  //   43eb6 42c00 43a0e 8165c 84682 8092a 83907 41f89 817b0 40855 82056 425e8 43ff2 8039f 42bd7 82137
  //   4416b 40273 8324a 814e4 44570 41c0f 429da 82640 8069c 8099e 414d5 41004 81beb 84113 419b1 81add
  //   83f35 425ff 829cd 40250 82945 4366d 40cc2 444f8 80814 81156 8446d 42a82 42bae 82578 41135 405d0
  //   8304b 82b3a 40972 822ba 4443a 42337 82506 80bd3 80560 83552 83955 81434 43096 43da1 81aa2 80305
  //   428e6 428cc 808a2 40e80 845f0 4215d 82765 82e29 40be5 82b74 42715 417a2 41fab 8452f 81c0a 83325
  //   44624 80205 42dfc 41333 40958 81348 42736 41069 84510 44669 826dd 8067e 408e4 44680 444e8 832ad
  //   821f8 83509 82d46 81184 432cd 80b77 4005a 440e0 81ea0 43d73 42b8c 80624 41468 42699 415ed 80fc1 0
  //   100000
endmodule

module Checker (
  input  [9:0] TestNumber,
  input  [7:0] YourByteRead,
  output CmdIsRead,
  output [7:0] CorrectByteRead,
  output Correct
);

  wire comparator_1_eq;
  wire [9:0] subtractor_1_out;

  // Probe on TestNumber
  Subtractor #(.width(10)) subtractor_1 (.a(TestNumber), .b(10'h1), .out(subtractor_1_out));  // open: bin, bout
  ROM #(.addrWidth(10), .dataWidth(9)) rom_1 (
    .addr(subtractor_1_out), .data({CmdIsRead, CorrectByteRead}));  // open: sel
  Comparator #(.mode("unsigned")) comparator_1 (
    .a(YourByteRead), .b(CorrectByteRead), .eq(comparator_1_eq));  // open: gt, lt
  and and_1 (Correct, comparator_1_eq, CmdIsRead);

  // Other names for the same wires on the sheet: Test_Number[9:0] = TestNumber

  // Notes on the sheet:
  //   Read Solutions
  //   contents of rom_1 (hex, n*v repeats v):
  //   1a3 1dc 6b 125 1 75 1dc 1c3 d8 1ab 77 70 b 33 10b d8 1c3 c9 174 58 bf 153 199 f 9d 56 1bb 13b 89 16c
  //   180 66 b6 0 e 107 1bf 1d8 167 89 118 55 1a2 e8 f2 1c3 d7 142 6b 73 1ab 18c 70 f da 1c3 14c 1d8 d5 4
  //   1d8 16b b1 1f4 1f2 ff 1da 50 1da 6d c2 f8 155 1c6 1f8 82 ae 1ff 35 d0 16b 1ae 72 175 3a 37 1ff 173
  //   1d0 158 167 1d5 96 a1 1f4 1c3 e6 cc 155 80 170 5d 1e6 166 e5 1ae 15 a2 ab 170 10f 13b 24 150 fc 33
  //   58 133 36 69 170 69 1c3 14c e4 80 e8 1ab 15d 158 1fc 135 cd 1e5 5a e0 104 73 8c 14c 68 99 ed 1a6
endmodule

module Set (
  input  CLK,
  input  [6:0] Tag,
  input  [1:0] Offset,
  input  Write2Cache,
  input  Set,
  input  AgeStart,
  input  NextAgeStart,
  input  [7:0] CpuWriteValue,
  input  [31:0] LineFromMem,
  input  NextLine,
  output [7:0] ByteRead,
  output DidContain,
  output Evict,
  output [6:0] TagOfEvictedLine,
  output [31:0] LineToWriteBack
);

  wire agesq, Contains0, Contains1, Contains2, Dirty0, Dirty1, Dirty2, Line0, Line1, Line2, NextAge,
       or_1_out, or_2_out, or_4_out, Write0, Write1, Write2;
  wire [1:0] adder_1_out, adder_2_out, adder_3_out, Age0, Age1, Age2, multiplexer_1_out, multiplexer_2_out,
       multiplexer_3_out, multiplexer_4_out, multiplexer_5_out, multiplexer_6_out, NewAge0, NewAge1, NewAge2,
       SelectedAge;
  wire [2:0] comparator_1_gt, comparator_2_gt, comparator_3_gt;
  wire [6:0] TEL0, TEL1, TEL2;
  wire [7:0] Byte0, Byte1, Byte2;
  wire [31:0] WriteBack0, WriteBack1, WriteBack2;

  and and_1 (Write0, Line0, Set);
  and and_2 (Write1, Line1, Set);
  and and_3 (Write2, Line2, Set);
  or or_1 (or_1_out, AgeStart, NextAge);
  and and_4 (NextAge, Set, NextAgeStart);
  Line line_1 (
    .CLK(CLK), .IntendedSet(Write0), .Write2Cache(Write2Cache), .Tag(Tag), .Offset(Offset),
    .ByteToWrite(CpuWriteValue), .Data(LineFromMem), .SetAge(or_1_out), .Age(NewAge0), .NextLine(NextLine),
    .Contains(Contains0), .CurrentData(Byte0), .CurrentAge(Age0), .TheTag(TEL0), .Dirty(Dirty0),
    .FullLine(WriteBack0));
  Eviction eviction_1 (
    .TEL0(TEL0), .TEL1(TEL1), .TEL2(TEL2), .Dirty0(Dirty0), .Dirty1(Dirty1), .Dirty2(Dirty2), .Age0(Age0),
    .Age1(Age1), .Age2(Age2), .DidContain(DidContain), .Contains0(Contains0), .Contains1(Contains1),
    .Contains2(Contains2), .WriteBack0(WriteBack0), .WriteBack1(WriteBack1), .WriteBack2(WriteBack2),
    .Byte0(Byte0), .Byte1(Byte1), .Byte2(Byte2), .ByteRead(ByteRead), .Evict(Evict),
    .TagOfEvictedLine(TagOfEvictedLine), .LineToWriteBack(LineToWriteBack), .SelectedAge(SelectedAge),
    .Line0(Line0), .Line1(Line1), .Line2(Line2));
  or or_2 (or_2_out, AgeStart, NextAge);
  Comparator #(.width(2), .mode("unsigned")) comparator_1 (
    .a(Age0), .b(SelectedAge), .gt(comparator_1_gt[0]), .eq(comparator_1_gt[2]), .lt(comparator_1_gt[1]));
  Comparator #(.width(2), .mode("unsigned")) comparator_2 (
    .a(Age1), .b(SelectedAge), .gt(comparator_2_gt[0]), .eq(comparator_2_gt[2]), .lt(comparator_2_gt[1]));
  Comparator #(.width(2), .mode("unsigned")) comparator_3 (
    .a(Age2), .b(SelectedAge), .gt(comparator_3_gt[0]), .eq(comparator_3_gt[2]), .lt(comparator_3_gt[1]));
  Line line_2 (
    .CLK(CLK), .IntendedSet(Write1), .Write2Cache(Write2Cache), .Tag(Tag), .Offset(Offset),
    .ByteToWrite(CpuWriteValue), .Data(LineFromMem), .SetAge(or_2_out), .Age(NewAge1), .NextLine(NextLine),
    .Contains(Contains1), .CurrentData(Byte1), .CurrentAge(Age1), .TheTag(TEL1), .Dirty(Dirty1),
    .FullLine(WriteBack1));
  Adder #(.width(2)) adder_1 (.a(Age0), .b(2'b01), .out(adder_1_out));  // open: cin, cout
  Adder #(.width(2)) adder_2 (.a(Age1), .b(2'b01), .out(adder_2_out));  // open: cin, cout
  Adder #(.width(2)) adder_3 (.a(Age2), .b(2'b01), .out(adder_3_out));  // open: cin, cout
  Multiplexer #(.select(3), .width(2)) multiplexer_1 (
    .in1(Age0), .in2(adder_1_out), .in4(2'b00), .out(multiplexer_1_out), .sel(comparator_1_gt));  // open: in0, in3, in5, in6, in7, en
  Multiplexer #(.select(3), .width(2), .enable("false")) multiplexer_2 (
    .in1(Age1), .in2(adder_2_out), .in4(2'b00), .out(multiplexer_2_out), .sel(comparator_2_gt));  // open: in0, in3, in5, in6, in7
  Multiplexer #(.select(3), .width(2), .enable("false")) multiplexer_3 (
    .in1(Age2), .in2(adder_3_out), .in4(2'b00), .out(multiplexer_3_out), .sel(comparator_3_gt));  // open: in0, in3, in5, in6, in7
  or or_3 (agesq, NextAge, AgeStart);
  Multiplexer #(.width(2), .enable("false")) multiplexer_4 (
    .in0(multiplexer_1_out), .in1(2'b00), .out(multiplexer_4_out), .sel(AgeStart));
  Multiplexer #(.width(2), .enable("false")) multiplexer_5 (
    .in0(multiplexer_2_out), .in1(2'b01), .out(multiplexer_5_out), .sel(AgeStart));
  Multiplexer #(.width(2), .enable("false")) multiplexer_6 (
    .in0(multiplexer_3_out), .in1(2'b10), .out(multiplexer_6_out), .sel(AgeStart));
  Multiplexer #(.width(2), .enable("false")) multiplexer_7 (
    .in0(Age0), .in1(multiplexer_4_out), .out(NewAge0), .sel(agesq));
  Multiplexer #(.width(2), .enable("false")) multiplexer_8 (
    .in0(Age1), .in1(multiplexer_5_out), .out(NewAge1), .sel(agesq));
  Multiplexer #(.width(2), .enable("false")) multiplexer_9 (
    .in0(Age2), .in1(multiplexer_6_out), .out(NewAge2), .sel(agesq));
  or or_4 (or_4_out, AgeStart, NextAge);
  Line line_3 (
    .CLK(CLK), .IntendedSet(Write2), .Write2Cache(Write2Cache), .Tag(Tag), .Offset(Offset),
    .ByteToWrite(CpuWriteValue), .Data(LineFromMem), .SetAge(or_4_out), .Age(NewAge2), .NextLine(NextLine),
    .Contains(Contains2), .CurrentData(Byte2), .CurrentAge(Age2), .TheTag(TEL2), .Dirty(Dirty2),
    .FullLine(WriteBack2));
  or or_5 (DidContain, Contains0, Contains1, Contains2);

  // Other names for the same wires on the sheet: MainLineToWriteBack[31:0] = LineToWriteBack

  // Notes on the sheet:
  //   Make sure that this set's ages need to be updated
  //   Since there are three ways per set, initialize them here:
endmodule

module Line (
  input  CLK,
  input  IntendedSet,
  input  Write2Cache,
  input  [6:0] Tag,
  input  [1:0] Offset,
  input  [7:0] ByteToWrite,
  input  [31:0] Data,
  input  SetAge,
  input  [1:0] Age,
  input  NextLine,
  output Contains,
  output [7:0] CurrentData,
  output [1:0] CurrentAge,
  output [6:0] TheTag,
  output Dirty,
  output [31:0] FullLine
);

  wire comparator_1_eq, comparator_2_eq, comparator_3_eq, comparator_4_eq, comparator_5_eq, Modified,
       ModifyData, UpdateAndSet, Valid;

  and and_1 (ModifyData, IntendedSet, Write2Cache);
  and and_2 (UpdateAndSet, IntendedSet, NextLine);
  Multiplexer #(.select(2), .width(8), .enable("false")) multiplexer_1 (
    .in0(FullLine[7:0]), .in1(FullLine[15:8]), .in2(FullLine[23:16]), .in3(FullLine[31:24]),
    .out(CurrentData), .sel(Offset));
  Comparator #(.width(7), .mode("unsigned")) comparator_1 (.a(Tag), .b(TheTag), .eq(comparator_1_eq));  // open: gt, lt
  and and_3 (Contains, comparator_1_eq, Valid);
  or or_1 (Modified, ModifyData, UpdateAndSet);
  Comparator #(.width(2), .mode("unsigned")) comparator_2 (
    .a(Offset), .b(2'b00), .eq(comparator_2_eq));  // open: gt, lt
  Comparator #(.width(2), .mode("unsigned")) comparator_3 (
    .a(Offset), .b(2'b10), .eq(comparator_3_eq));  // open: gt, lt
  ByteData Byte0 (
    .OffsetAndx(comparator_2_eq), .Byte(ByteToWrite), .DataToWriteAtx(Data[7:0]), .Write2Cache(Write2Cache),
    .UpdateAndSet(UpdateAndSet), .ModifyData(ModifyData), .CLK(CLK), .ByteVal(FullLine[7:0]));
  ByteData Byte2 (
    .OffsetAndx(comparator_3_eq), .Byte(ByteToWrite), .DataToWriteAtx(Data[23:16]),
    .Write2Cache(Write2Cache), .UpdateAndSet(UpdateAndSet), .ModifyData(ModifyData), .CLK(CLK),
    .ByteVal(FullLine[23:16]));
  Register #(.width(1)) u_Dirty (.D(ModifyData), .en(Modified), .Q(Dirty), .clk(CLK));  // open: clr
  Register #(.width(1)) u_Valid (.D(1'b1), .en(Modified), .Q(Valid), .clk(CLK));  // open: clr
  Comparator #(.width(2), .mode("unsigned")) comparator_4 (
    .a(Offset), .b(2'b01), .eq(comparator_4_eq));  // open: gt, lt
  Comparator #(.width(2), .mode("unsigned")) comparator_5 (
    .a(Offset), .b(2'b11), .eq(comparator_5_eq));  // open: gt, lt
  Register #(.width(7)) u_Tag (.D(Tag), .en(Modified), .Q(TheTag), .clk(CLK));  // open: clr
  ByteData Byte1 (
    .OffsetAndx(comparator_4_eq), .Byte(ByteToWrite), .DataToWriteAtx(Data[15:8]), .Write2Cache(Write2Cache),
    .UpdateAndSet(UpdateAndSet), .ModifyData(ModifyData), .CLK(CLK), .ByteVal(FullLine[15:8]));
  ByteData Byte3 (
    .OffsetAndx(comparator_5_eq), .Byte(ByteToWrite), .DataToWriteAtx(Data[31:24]),
    .Write2Cache(Write2Cache), .UpdateAndSet(UpdateAndSet), .ModifyData(ModifyData), .CLK(CLK),
    .ByteVal(FullLine[31:24]));
  Register #(.width(2)) u_Age (.D(Age), .en(SetAge), .Q(CurrentAge), .clk(CLK));  // open: clr

  // Other names for the same wires on the sheet: AgeSave[1:0] = CurrentAge; CurTag[6:0] = TheTag;
  //   DataWrite0[7:0] = Data[7:0]; DataWrite1[7:0] = Data[15:8]; DataWrite2[7:0] = Data[23:16];
  //   DataWrite3[7:0] = Data[31:24]; Byte0Data[7:0] = FullLine[7:0]; Byte1Data[7:0] = FullLine[15:8];
  //   Byte2Data[7:0] = FullLine[23:16]; Byte3Data[7:0] = FullLine[31:24]; RightSet = IntendedSet
endmodule

// NS3
module NextState3 (
  input  P3,
  input  P2,
  input  P1,
  input  Contains,
  input  Dirty,
  input  Read,
  input  Write,
  output P3p
);

  wire and_1_out, and_2_out, and_3_out, and_4_out, and_5_out, and_6_out, and_7_out, not_1_out, not_2_out,
       not_3_out, not_4_out, not_5_out, not_6_out, not_7_out, not_8_out, not_9_out, not_10_out, not_11_out,
       not_12_out, not_13_out, not_14_out, not_15_out, not_16_out;

  not not_1 (not_1_out, P1);
  not not_2 (not_2_out, Dirty);
  not not_3 (not_3_out, Read);
  not not_4 (not_4_out, P1);
  not not_5 (not_5_out, Dirty);
  not not_6 (not_6_out, Write);
  not not_7 (not_7_out, P3);
  not not_8 (not_8_out, Read);
  not not_9 (not_9_out, P3);
  not not_10 (not_10_out, Write);
  not not_11 (not_11_out, P2);
  not not_12 (not_12_out, Write);
  not not_13 (not_13_out, P1);
  not not_14 (not_14_out, Read);
  not not_15 (not_15_out, P1);
  not not_16 (not_16_out, Write);
  and and_1 (and_1_out, P2, not_1_out, not_2_out, not_3_out, Write);
  and and_2 (and_2_out, P2, not_4_out, not_5_out, Read, not_6_out);
  and and_3 (and_3_out, not_7_out, P2, P1, not_8_out, Write);
  and and_4 (and_4_out, not_9_out, P2, P1, Read, not_10_out);
  and and_5 (and_5_out, P3, not_11_out, P1, Read, not_12_out);
  and and_6 (and_6_out, P3, P2, not_13_out, not_14_out, Write);
  and and_7 (and_7_out, P3, P2, not_15_out, Read, not_16_out);
  or or_1 (P3p, and_1_out, and_2_out, and_3_out, and_4_out, and_5_out, and_6_out, and_7_out);
endmodule

// NS2
module NextState2 (
  input  P3,
  input  P2,
  input  P1,
  input  Contains,
  input  Dirty,
  input  Read,
  input  Write,
  output P2p
);

  wire and_1_out, and_2_out, and_3_out, and_4_out, and_5_out, and_6_out, and_7_out, and_8_out, and_9_out,
       and_10_out, and_11_out, and_12_out, not_1_out, not_2_out, not_3_out, not_4_out, not_5_out, not_6_out,
       not_7_out, not_8_out, not_9_out, not_10_out, not_11_out, not_12_out, not_13_out, not_14_out,
       not_15_out, not_16_out, not_17_out, not_18_out, not_19_out, not_20_out, not_21_out, not_22_out,
       not_23_out, not_24_out, not_25_out, not_26_out, not_27_out, not_28_out, not_29_out, not_30_out,
       not_31_out, not_32_out, not_33_out, not_34_out, not_35_out;

  not not_1 (not_1_out, P3);
  not not_2 (not_2_out, P2);
  not not_3 (not_3_out, Contains);
  not not_4 (not_4_out, Read);
  not not_5 (not_5_out, P3);
  not not_6 (not_6_out, P2);
  not not_7 (not_7_out, Dirty);
  not not_8 (not_8_out, Read);
  not not_9 (not_9_out, P3);
  not not_10 (not_10_out, P2);
  not not_11 (not_11_out, Dirty);
  not not_12 (not_12_out, Write);
  not not_13 (not_13_out, P3);
  not not_14 (not_14_out, P2);
  not not_15 (not_15_out, Read);
  not not_16 (not_16_out, Write);
  not not_17 (not_17_out, P3);
  not not_18 (not_18_out, Contains);
  not not_19 (not_19_out, Write);
  not not_20 (not_20_out, P1);
  not not_21 (not_21_out, Dirty);
  not not_22 (not_22_out, Read);
  not not_23 (not_23_out, P1);
  not not_24 (not_24_out, Dirty);
  not not_25 (not_25_out, Write);
  not not_26 (not_26_out, P3);
  not not_27 (not_27_out, Read);
  not not_28 (not_28_out, P3);
  not not_29 (not_29_out, Write);
  not not_30 (not_30_out, P2);
  not not_31 (not_31_out, Read);
  not not_32 (not_32_out, P1);
  not not_33 (not_33_out, Read);
  not not_34 (not_34_out, P1);
  not not_35 (not_35_out, Write);
  and and_1 (and_1_out, not_1_out, not_2_out, P1, not_3_out, not_4_out);
  and and_2 (and_2_out, not_5_out, not_6_out, P1, not_7_out, not_8_out);
  and and_3 (and_3_out, not_9_out, not_10_out, P1, not_11_out, not_12_out);
  and and_4 (and_4_out, not_13_out, not_14_out, P1, not_15_out, not_16_out);
  and and_5 (and_5_out, not_17_out, P1, not_18_out, Read, not_19_out);
  and and_6 (and_6_out, P2, not_20_out, not_21_out, not_22_out, Write);
  and and_7 (and_7_out, P2, not_23_out, not_24_out, Read, not_25_out);
  and and_8 (and_8_out, not_26_out, P2, P1, not_27_out, Write);
  and and_9 (and_9_out, not_28_out, P2, P1, Read, not_29_out);
  and and_10 (and_10_out, P3, not_30_out, P1, not_31_out, Write);
  and and_11 (and_11_out, P3, P2, not_32_out, not_33_out, Write);
  and and_12 (and_12_out, P3, P2, not_34_out, Read, not_35_out);
  or or_1 (P2p, and_1_out, and_2_out, and_3_out, and_4_out, and_5_out, and_6_out, and_7_out, and_8_out, and_9_out, and_10_out, and_11_out, and_12_out);
endmodule

// NS1
module NextState1 (
  input  P3,
  input  P2,
  input  P1,
  input  Contains,
  input  Dirty,
  input  Read,
  input  Write,
  output P1p
);

  wire and_1_out, and_2_out, and_3_out, and_4_out, and_5_out, and_6_out, and_7_out, and_8_out, and_9_out,
       and_10_out, and_11_out, and_12_out, and_13_out, not_1_out, not_2_out, not_3_out, not_4_out, not_5_out,
       not_6_out, not_7_out, not_8_out, not_9_out, not_10_out, not_11_out, not_12_out, not_13_out,
       not_14_out, not_15_out, not_16_out, not_17_out, not_18_out, not_19_out, not_20_out, not_21_out,
       not_22_out, not_23_out, not_24_out, not_25_out, not_26_out, not_27_out, not_28_out, not_29_out,
       not_30_out, not_31_out, not_32_out, not_33_out, not_34_out, not_35_out, not_36_out, not_37_out;

  not not_1 (not_1_out, P3);
  not not_2 (not_2_out, P2);
  not not_3 (not_3_out, P1);
  not not_4 (not_4_out, P3);
  not not_5 (not_5_out, P2);
  not not_6 (not_6_out, Contains);
  not not_7 (not_7_out, Read);
  not not_8 (not_8_out, P3);
  not not_9 (not_9_out, P2);
  not not_10 (not_10_out, Contains);
  not not_11 (not_11_out, Write);
  not not_12 (not_12_out, P3);
  not not_13 (not_13_out, P2);
  not not_14 (not_14_out, Read);
  not not_15 (not_15_out, Write);
  not not_16 (not_16_out, P1);
  not not_17 (not_17_out, Contains);
  not not_18 (not_18_out, Read);
  not not_19 (not_19_out, P1);
  not not_20 (not_20_out, Contains);
  not not_21 (not_21_out, Write);
  not not_22 (not_22_out, P3);
  not not_23 (not_23_out, Dirty);
  not not_24 (not_24_out, Read);
  not not_25 (not_25_out, P3);
  not not_26 (not_26_out, Dirty);
  not not_27 (not_27_out, Write);
  not not_28 (not_28_out, P3);
  not not_29 (not_29_out, Read);
  not not_30 (not_30_out, P3);
  not not_31 (not_31_out, Write);
  not not_32 (not_32_out, P2);
  not not_33 (not_33_out, Read);
  not not_34 (not_34_out, P1);
  not not_35 (not_35_out, Read);
  not not_36 (not_36_out, P1);
  not not_37 (not_37_out, Write);
  and and_1 (and_1_out, not_1_out, not_2_out, not_3_out);
  and and_2 (and_2_out, not_4_out, not_5_out, not_6_out, not_7_out);
  and and_3 (and_3_out, not_8_out, not_9_out, not_10_out, not_11_out);
  and and_4 (and_4_out, not_12_out, not_13_out, not_14_out, not_15_out);
  and and_5 (and_5_out, not_16_out, not_17_out, Dirty, not_18_out, Write);
  and and_6 (and_6_out, not_19_out, not_20_out, Dirty, Read, not_21_out);
  and and_7 (and_7_out, not_22_out, Contains, not_23_out, not_24_out, Write);
  and and_8 (and_8_out, not_25_out, Contains, not_26_out, Read, not_27_out);
  and and_9 (and_9_out, not_28_out, P2, P1, not_29_out, Write);
  and and_10 (and_10_out, not_30_out, P2, P1, Read, not_31_out);
  and and_11 (and_11_out, P3, not_32_out, not_33_out, Write);
  and and_12 (and_12_out, P3, not_34_out, not_35_out, Write);
  and and_13 (and_13_out, P3, not_36_out, Read, not_37_out);
  or or_1 (P1p, and_1_out, and_2_out, and_3_out, and_4_out, and_5_out, and_6_out, and_7_out, and_8_out, and_9_out, and_10_out, and_11_out, and_12_out, and_13_out);
endmodule

module Control (
  input  CurrContain,
  input  Dirty,
  input  CpuRead,
  input  CpuWrite,
  input  CLK,
  output Ready,
  output AgesStart,
  output NextAgeStart,
  output Write2Cache,
  output MemRead,
  output NextLine,
  output MemWrite,
  output [2:0] state
);

  wire P1p, P2p, P3p;

  NextState3 nextstate3_1 (
    .P3(state[2]), .P2(state[1]), .P1(state[0]), .Contains(CurrContain), .Dirty(Dirty), .Read(CpuRead),
    .Write(CpuWrite), .P3p(P3p));
  T_Flip_Flop t_ff_1 (.clk(CLK), .T(P3p), .Q(state[2]));  // open: Qn, preset, reset, en
  T_Flip_Flop t_ff_2 (.clk(CLK), .T(P2p), .Q(state[1]));  // open: Qn, preset, reset, en
  NextState2 nextstate2_1 (
    .P3(state[2]), .P2(state[1]), .P1(state[0]), .Contains(CurrContain), .Dirty(Dirty), .Read(CpuRead),
    .Write(CpuWrite), .P2p(P2p));
  T_Flip_Flop t_ff_3 (.clk(CLK), .T(P1p), .Q(state[0]));  // open: Qn, preset, reset, en
  Output output_1 (
    .P3(state[2]), .P1(state[1]), .P2(state[0]), .Ready(Ready), .AgesStart(AgesStart),
    .NextAgeStart(NextAgeStart), .Write2Cache(Write2Cache), .MemRead(MemRead), .NextLine(NextLine),
    .MemWrite(MemWrite));
  NextState1 nextstate1_1 (
    .P3(state[2]), .P2(state[1]), .P1(state[0]), .Contains(CurrContain), .Dirty(Dirty), .Read(CpuRead),
    .Write(CpuWrite), .P1p(P1p));

  // Other names for the same wires on the sheet: P1 = state[0]; P2 = state[1]; P3 = state[2]
endmodule

module Output (
  input  P3,
  input  P1,
  input  P2,
  output Ready,
  output AgesStart,
  output NextAgeStart,
  output Write2Cache,
  output MemRead,
  output NextLine,
  output MemWrite
);

  wire not_1_out, not_2_out, not_3_out, not_4_out, not_5_out, not_6_out, not_7_out, not_8_out, not_9_out,
       not_10_out;

  not not_1 (not_1_out, P3);
  not not_2 (not_2_out, P1);
  not not_3 (not_3_out, P3);
  not not_4 (not_4_out, P1);
  not not_5 (not_5_out, P2);
  not not_6 (not_6_out, P1);
  not not_7 (not_7_out, P2);
  not not_8 (not_8_out, P1);
  not not_9 (not_9_out, P2);
  not not_10 (not_10_out, P3);
  and and_1 (Ready, not_1_out, not_2_out, P2);
  and and_2 (AgesStart, not_3_out, not_4_out, not_5_out);
  and and_3 (NextAgeStart, P3, not_6_out, P2);
  and and_4 (Write2Cache, P3, P1, not_7_out);
  and and_5 (MemRead, P3, not_8_out, not_9_out);
  and and_6 (MemWrite, not_10_out, P1, P2);

  assign NextLine = MemRead;
endmodule

module ByteData (
  input  OffsetAndx,
  input  [7:0] Byte,
  input  [7:0] DataToWriteAtx,
  input  Write2Cache,
  input  UpdateAndSet,
  input  ModifyData,
  input  CLK,
  output [7:0] ByteVal
);

  wire and_1_out, and_2_out, or_1_out;
  wire [7:0] multiplexer_1_out;

  and and_1 (and_1_out, Write2Cache, OffsetAndx);
  Multiplexer #(.width(8), .enable("false")) multiplexer_1 (
    .in0(DataToWriteAtx), .in1(Byte), .out(multiplexer_1_out), .sel(and_1_out));
  and and_2 (and_2_out, ModifyData, OffsetAndx);
  or or_1 (or_1_out, and_2_out, UpdateAndSet);
  Register u_Byte (.D(multiplexer_1_out), .en(or_1_out), .Q(ByteVal), .clk(CLK));  // open: clr
endmodule

module Eviction (
  input  [6:0] TEL0,
  input  [6:0] TEL1,
  input  [6:0] TEL2,
  input  Dirty0,
  input  Dirty1,
  input  Dirty2,
  input  [1:0] Age0,
  input  [1:0] Age1,
  input  [1:0] Age2,
  input  DidContain,
  input  Contains0,
  input  Contains1,
  input  Contains2,
  input  [31:0] WriteBack0,
  input  [31:0] WriteBack1,
  input  [31:0] WriteBack2,
  input  [7:0] Byte0,
  input  [7:0] Byte1,
  input  [7:0] Byte2,
  output [7:0] ByteRead,
  output Evict,
  output [6:0] TagOfEvictedLine,
  output [31:0] LineToWriteBack,
  output [1:0] SelectedAge,
  output Line0,
  output Line1,
  output Line2
);

  wire comparator_4_eq, comparator_5_eq, comparator_6_eq, comparator_7_eq, comparator_8_eq, comparator_9_eq,
       DDirty, not_1_out;
  wire [1:0] LineFound, multiplexer_6_out, multiplexer_7_out, multiplexer_8_out;
  wire [2:0] comparator_1_eq;

  Comparator #(.width(2), .mode("unsigned")) comparator_1 (
    .a(Age0), .b(2'b10), .eq(comparator_1_eq[0]));  // open: gt, lt
  Comparator #(.width(2), .mode("unsigned")) comparator_2 (
    .a(Age1), .b(2'b10), .eq(comparator_1_eq[1]));  // open: gt, lt
  Comparator #(.width(2), .mode("unsigned")) comparator_3 (
    .a(Age2), .b(2'b10), .eq(comparator_1_eq[2]));  // open: gt, lt
  Multiplexer #(.select(3)) multiplexer_1 (
    .in0(1'b0), .in1(Dirty0), .in2(Dirty1), .in4(Dirty2), .out(DDirty), .sel(comparator_1_eq));  // open: in3, in5, in6, in7, en
  Comparator #(.width(2), .mode("unsigned")) comparator_4 (.a(Age0), .b(2'b10), .eq(comparator_4_eq));  // open: gt, lt
  Comparator #(.width(2), .mode("unsigned")) comparator_5 (
    .a(SelectedAge), .b(Age0), .eq(comparator_5_eq));  // open: gt, lt
  Comparator #(.width(2), .mode("unsigned")) comparator_6 (.a(Age1), .b(2'b10), .eq(comparator_6_eq));  // open: gt, lt
  Comparator #(.width(2), .mode("unsigned")) comparator_7 (
    .a(SelectedAge), .b(Age1), .eq(comparator_7_eq));  // open: gt, lt
  Comparator #(.width(2), .mode("unsigned")) comparator_8 (.a(Age2), .b(2'b10), .eq(comparator_8_eq));  // open: gt, lt
  Comparator #(.width(2), .mode("unsigned")) comparator_9 (
    .a(SelectedAge), .b(Age2), .eq(comparator_9_eq));  // open: gt, lt
  Multiplexer #(.enable("false")) multiplexer_2 (
    .in0(comparator_4_eq), .in1(comparator_5_eq), .out(Line0), .sel(DidContain));
  Multiplexer #(.enable("false")) multiplexer_3 (
    .in0(comparator_6_eq), .in1(comparator_7_eq), .out(Line1), .sel(DidContain));
  Multiplexer #(.enable("false")) multiplexer_4 (
    .in0(comparator_8_eq), .in1(comparator_9_eq), .out(Line2), .sel(DidContain));
  Multiplexer #(.select(3), .width(2)) multiplexer_5 (
    .in0(2'b00), .in1(2'b00), .in2(2'b01), .in4(2'b10), .out(LineFound),
    .sel({Contains2, Contains1, Contains0}));  // open: in3, in5, in6, in7, en
  Multiplexer #(.select(3), .width(2), .enable("false")) multiplexer_6 (
    .in0(2'b00), .in1(Age0), .in2(Age1), .in4(Age2), .out(multiplexer_6_out), .sel({Line2, Line1, Line0}));  // open: in3, in5, in6, in7
  Multiplexer #(.select(3), .width(2), .enable("false")) multiplexer_7 (
    .in0(2'b00), .in1(2'b00), .in2(2'b01), .in4(2'b10), .out(multiplexer_7_out), .sel({Line2, Line1, Line0}));  // open: in3, in5, in6, in7
  Multiplexer #(.select(2), .width(2), .enable("false")) multiplexer_8 (
    .in0(Age0), .in1(Age1), .in2(Age2), .out(multiplexer_8_out), .sel(LineFound));  // open: in3
  Multiplexer #(.width(2), .enable("false")) multiplexer_9 (
    .in0(multiplexer_6_out), .in1(multiplexer_8_out), .out(SelectedAge), .sel(DidContain));
  Multiplexer #(.select(2), .width(7), .enable("false")) multiplexer_10 (
    .in0(TEL0), .in1(TEL1), .in2(TEL2), .out(TagOfEvictedLine), .sel(multiplexer_7_out));  // open: in3
  Multiplexer #(.select(2), .width(32), .enable("false")) multiplexer_11 (
    .in0(WriteBack0), .in1(WriteBack1), .in2(WriteBack2), .out(LineToWriteBack), .sel(multiplexer_7_out));  // open: in3
  not not_1 (not_1_out, DidContain);
  and and_1 (Evict, not_1_out, DDirty);
  Multiplexer #(.select(2), .width(8), .enable("false")) multiplexer_12 (
    .in0(Byte0), .in1(Byte1), .in2(Byte2), .out(ByteRead), .sel(multiplexer_7_out));  // open: in3

  // Other names for the same wires on the sheet: MainLineToWriteBack[31:0] = LineToWriteBack
endmodule
