// Logisim project 4bitAdder.circ as structural Verilog: 4 circuits, main circuit main
// Number Correct
module main (
  input  Enable_Halt
);

  wire and_2_out, CLK, Correct, Halt, not_1_out, not_2_out, NotDone, YourCout;
  wire [3:0] A, B, YourSum;
  wire [4:0] Solution;
  wire [8:0] Number_Correct_q;

  not not_1 (not_1_out, Correct);
  and and_1 (Halt, Enable_Halt, not_1_out);
  Clock clock_1 (.out(CLK));
  Inputs inputs_1 (.Halt(Halt), .Clk(CLK), .A(A), .B(B), .NotDone(NotDone));
  // Probe on A
  // Probe on B
  // Probe on YourSum
  // Probe on YourCout
  // Probe on Solution[3:0]
  // Probe on Solution[4]
  _4bitAdder _4BitAdder (.A(A), .B(B), .Cin(1'b0), .Sum(YourSum), .Cout(YourCout));
  not not_2 (not_2_out, Halt);
  and and_2 (and_2_out, Correct, NotDone, not_2_out);
  Checker checker_1 (.A(A), .B(B), .Sum(YourSum), .Cout(YourCout), .Correct(Correct), .CorrectAnswer(Solution));
  Counter #(.width(9), .max('h100)) Number_Correct (
    .count(and_2_out), .Q(Number_Correct_q), .clk(CLK));  // open: load, D, carry, clr
  // Probe on Number_Correct_q

  // Notes on the sheet:
  //   Use the Poke Tool on the enable halt input to enable/disable halting
  //   Enabling Halt will cause the testing to stop as soon as the first incorrect answer is detected
endmodule

module _4bitAdder (
  input  [3:0] A,
  input  [3:0] B,
  input  Cin,
  output [3:0] Sum,
  output Cout
);

  wire and_1_out, and_2_out, and_3_out, and_4_out, and_5_out, and_6_out, and_7_out, and_8_out, or_1_out,
       or_2_out, or_4_out, xor_1_out, xor_2_out, xor_3_out, xor_4_out;

  xor xor_1 (xor_1_out, A[0], B[0]);
  and and_1 (and_1_out, A[0], B[0]);
  xor xor_2 (xor_2_out, A[1], B[1]);
  and and_2 (and_2_out, A[1], B[1]);
  xor xor_3 (xor_3_out, A[2], B[2]);
  and and_3 (and_3_out, A[2], B[2]);
  xor xor_4 (xor_4_out, A[3], B[3]);
  and and_4 (and_4_out, A[3], B[3]);
  and and_5 (and_5_out, Cin, xor_1_out);
  or or_1 (or_1_out, and_5_out, and_1_out);
  and and_6 (and_6_out, or_4_out, xor_4_out);
  and and_7 (and_7_out, or_1_out, xor_2_out);
  or or_2 (or_2_out, and_7_out, and_2_out);
  and and_8 (and_8_out, xor_3_out, or_2_out);
  or or_3 (Cout, and_6_out, and_4_out);
  or or_4 (or_4_out, and_8_out, and_3_out);
  xor xor_5 (Sum[0], Cin, xor_1_out);
  xor xor_6 (Sum[1], or_1_out, xor_2_out);
  xor xor_7 (Sum[2], or_2_out, xor_3_out);
  xor xor_8 (Sum[3], or_4_out, xor_4_out);
endmodule

module Inputs (
  input  Halt,
  input  Clk,
  output [3:0] A,
  output [3:0] B,
  output NotDone
);

  wire A_carry, and_1_out, and_2_out, and_3_out, and_4_out, CarryB, Delay_q, nHalt;

  not not_1 (nHalt, Halt);
  and and_1 (and_1_out, nHalt, NotDone);
  Counter #(.width(4), .max('hf)) u_B (.count(and_1_out), .Q(B), .carry(CarryB), .clk(Clk));  // open: load, D, clr
  and and_2 (and_2_out, nHalt, CarryB);
  Counter #(.width(4), .max('hf), .ongoal("stay")) u_A (
    .count(and_2_out), .Q(A), .carry(A_carry), .clk(Clk));  // open: load, D, clr
  and and_3 (and_3_out, CarryB, A_carry);
  Register #(.width(1)) Delay (.D(and_3_out), .en(and_4_out), .Q(Delay_q), .clk(Clk));  // open: clr
  and and_4 (and_4_out, nHalt, NotDone);
  not not_2 (NotDone, Delay_q);
endmodule

module Checker (
  input  [3:0] A,
  input  [3:0] B,
  input  [3:0] Sum,
  input  Cout,
  output Correct,
  output [4:0] CorrectAnswer
);

  ROM #(.dataWidth(5)) rom_1 (.addr({A, B}), .data(CorrectAnswer));  // open: sel
  Comparator #(.width(5), .mode("unsigned")) comparator_1 (
    .a(CorrectAnswer), .b({Cout, Sum}), .eq(Correct));  // open: gt, lt

  // Other names for the same wires on the sheet: StudentSol[4:0] = {Cout, Sum}

  // Notes on the sheet:
  //   contents of rom_1 (hex, n*v repeats v):
  //   0 1 2 3 4 5 6 7 8 9 a b c d e f 1 2 3 4 5 6 7 8 9 a b c d e f 10 2 3 4 5 6 7 8 9 a b c d e f 10 11 3
  //   4 5 6 7 8 9 a b c d e f 10 11 12 4 5 6 7 8 9 a b c d e f 10 11 12 13 5 6 7 8 9 a b c d e f 10 11 12
  //   13 14 6 7 8 9 a b c d e f 10 11 12 13 14 15 7 8 9 a b c d e f 10 11 12 13 14 15 16 8 9 a b c d e f
  //   10 11 12 13 14 15 16 17 9 a b c d e f 10 11 12 13 14 15 16 17 18 a b c d e f 10 11 12 13 14 15 16 17
  //   18 19 b c d e f 10 11 12 13 14 15 16 17 18 19 1a c d e f 10 11 12 13 14 15 16 17 18 19 1a 1b d e f
  //   10 11 12 13 14 15 16 17 18 19 1a 1b 1c e f 10 11 12 13 14 15 16 17 18 19 1a 1b 1c 1d f 10 11 12 13
  //   14 15 16 17 18 19 1a 1b 1c 1d 1e
endmodule
