// Logisim project 4BitParity.circ as structural Verilog: 6 circuits, main circuit main
module main (
  input  Halt_Enable
);

  wire and_2_out, CLK, Correct, Done_Testing, Halt, Input, not_1_out, not_2_out, not_3_out, Solution,
       YourAnswer;
  wire [6:0] counter_1_q, TestNumber;

  not not_1 (not_1_out, Correct);
  Clock clock_1 (.out(CLK));
  and and_1 (Halt, Halt_Enable, not_1_out);
  Inputs inputs_1 (.Halt(Halt), .CLK(CLK), .Input(Input), .TestNumber(TestNumber), .Done_Testing(Done_Testing));
  _4BitEvenParity u_4bitevenparity_1 (.Input(Input), .CLK(CLK), .Is_Even(YourAnswer));
  // Probe on Input
  // Probe on YourAnswer
  // Probe on Solution
  // Probe on Correct
  not not_2 (not_2_out, Halt);
  and and_2 (and_2_out, Correct, not_2_out, not_3_out);
  not not_3 (not_3_out, Done_Testing);
  Checker checker_1 (.Your_Answer(YourAnswer), .TestNumber(TestNumber), .Correct(Correct), .Solution(Solution));
  Counter #(.width(7), .max('h41), .ongoal("stay")) counter_1 (
    .count(and_2_out), .Q(counter_1_q), .clk(CLK));  // open: load, D, carry, clr
  // Probe on counter_1_q

  // Notes on the sheet:
  //   Max 65
endmodule

module _4BitEvenParity (
  input  Input,
  input  CLK,
  output Is_Even
);

  wire S0, S0P, S1, S1P, S2, S2P;

  next_state next_state_1 (.S2(S2), .S1(S1), .S0(S0), .Input(Input), .S2P(S2P), .S1P(S1P), .S0P(S0P));
  Register #(.width(3)) register_1 (.D({S2P, S1P, S0P}), .Q({S2, S1, S0}), .clk(CLK));  // open: en, clr
  \output  output_1 (.S2(S2), .S1(S1), .S0(S0), .Is_Even(Is_Even));
endmodule

module Inputs (
  input  Halt,
  input  CLK,
  output Input,
  output [6:0] TestNumber,
  output Done_Testing
);

  wire not_1_out;

  not not_1 (not_1_out, Halt);
  Counter #(.width(7), .max('h41), .ongoal("stay")) counter_1 (
    .count(not_1_out), .Q(TestNumber), .carry(Done_Testing), .clk(CLK));  // open: load, D, clr
  ROM #(.addrWidth(7), .dataWidth(1)) rom_1 (.addr(TestNumber), .data(Input));  // open: sel

  // Notes on the sheet:
  //   contents of rom_1 (hex, n*v repeats v):
  //   7*0 1 0 0 1 0 0 0 1 1 0 1 0 0 0 1 0 1 0 1 1 0 0 4*1 0 0 0 1 0 0 1 1 0 1 0 1 0 4*1 0 0 1 1 0 4*1 0
  //   4*1
endmodule

module Checker (
  input  Your_Answer,
  input  [6:0] TestNumber,
  output Correct,
  output Solution
);

  ROM #(.addrWidth(7), .dataWidth(1)) rom_1 (.addr(TestNumber), .data(Solution));  // open: sel
  Comparator #(.width(1)) comparator_1 (.a(Solution), .b(Your_Answer), .eq(Correct));  // open: gt, lt

  // Notes on the sheet:
  //   contents of rom_1 (hex, n*v repeats v):
  //   4*0 1 11*0 1 7*0 1 0 0 0 1 11*0 1 0 0 0 1 7*0 1 11*0 1
endmodule

module next_state (
  input  S2,
  input  S1,
  input  S0,
  input  Input,
  output S2P,
  output S1P,
  output S0P
);

  wire and_1_out, and_2_out, and_3_out, and_4_out, and_5_out, and_6_out, and_7_out, not_1_out, not_2_out,
       not_3_out, not_4_out, not_5_out, not_6_out, not_8_out, not_9_out, not_10_out;

  not not_1 (not_1_out, S2);
  and and_1 (and_1_out, not_1_out, not_2_out, Input);
  not not_2 (not_2_out, S1);
  not not_3 (not_3_out, S1);
  and and_2 (and_2_out, not_3_out, S0, Input);
  and and_3 (and_3_out, S1, not_4_out);
  not not_4 (not_4_out, S0);
  not not_5 (not_5_out, S0);
  and and_4 (and_4_out, S2, not_5_out, not_6_out);
  not not_6 (not_6_out, Input);
  not not_7 (S1P, S1);
  not not_8 (not_8_out, S2);
  and and_5 (and_5_out, not_8_out, S1, Input);
  and and_6 (and_6_out, S2, not_9_out);
  not not_9 (not_9_out, S1);
  and and_7 (and_7_out, S2, not_10_out);
  not not_10 (not_10_out, Input);
  or or_1 (S2P, and_1_out, and_2_out, and_3_out, and_4_out);
  or or_2 (S0P, and_5_out, and_6_out, and_7_out);
endmodule

module \output  (
  input  S2,
  input  S1,
  input  S0,
  output Is_Even
);

  wire not_1_out, not_2_out;

  not not_1 (not_1_out, S2);
  not not_2 (not_2_out, S1);
  and and_1 (Is_Even, not_1_out, not_2_out, S0);
endmodule
