// Logisim project Vending.circ as structural Verilog: 6 circuits, main circuit main
module main (
  input  Halt_Enable
);

  wire and_2_out, CLK, Correct, Dime, Done_Testing, Give_Dime, Give_Merch, Give_Nickel, Halt, Nickel,
       not_1_out, not_2_out, not_3_out, Quarter, Sol_Give_Dime, Sol_Give_Merch, Sol_Give_Nickel;
  wire [8:0] counter_1_q, TestNumber;

  Clock clock_1 (.out(CLK));
  not not_1 (not_1_out, Correct);
  and and_1 (Halt, Halt_Enable, not_1_out);
  Inputs inputs_1 (
    .Halt(Halt), .CLK(CLK), .Quarter(Quarter), .Dime(Dime), .Nickel(Nickel), .TestNumber(TestNumber),
    .Done_Testing(Done_Testing));
  // Probe on Quarter
  // Probe on Dime
  // Probe on Nickel
  Vending vending_1 (
    .Quarter(Quarter), .Dime(Dime), .Nickel(Nickel), .CLK(CLK), .Give_Merchandise(Give_Merch),
    .Give_Dime(Give_Dime), .Give_Nickel(Give_Nickel));
  // Probe on Correct
  // Probe on Give_Merch
  // Probe on Sol_Give_Merch
  // Probe on Give_Dime
  // Probe on Sol_Give_Dime
  // Probe on Give_Nickel
  // Probe on Sol_Give_Nickel
  not not_2 (not_2_out, Halt);
  Checker checker_1 (
    .Give_Merch(Give_Merch), .Give_Dime(Give_Dime), .Give_Nickel(Give_Nickel), .TestNumber(TestNumber),
    .Correct(Correct), .Sol_Give_Merch(Sol_Give_Merch), .Sol_Give_Dime(Sol_Give_Dime),
    .Sol_Give_Nickel(Sol_Give_Nickel));
  and and_2 (and_2_out, Correct, not_2_out, not_3_out);
  not not_3 (not_3_out, Done_Testing);
  Counter #(.width(9), .max('h162), .ongoal("stay")) counter_1 (
    .count(and_2_out), .Q(counter_1_q), .clk(CLK));  // open: load, D, carry, clr
  // Probe on counter_1_q

  // Notes on the sheet:
  //   Max 354
endmodule

module Vending (
  input  Quarter,
  input  Dime,
  input  Nickel,
  input  CLK,
  output Give_Merchandise,
  output Give_Dime,
  output Give_Nickel
);

  wire S0, S0P, S1, S1P, S2, S2P;

  NextState nextstate_1 (
    .S2(S2), .S1(S1), .S0(S0), .Quarter(Quarter), .Dime(Dime), .Nickel(Nickel), .S2P(S2P), .S1P(S1P),
    .S0P(S0P));
  Register #(.width(3)) register_1 (.D({S2P, S1P, S0P}), .Q({S2, S1, S0}), .clk(CLK));  // open: en, clr
  Output output_1 (
    .S2(S2), .S1(S1), .S0(S0), .Quarter(Quarter), .Dime(Dime), .Nickel(Nickel),
    .Give_Merchandise(Give_Merchandise), .Give_Dime(Give_Dime), .Give_Nickel(Give_Nickel));
endmodule

module Inputs (
  input  Halt,
  input  CLK,
  output Quarter,
  output Dime,
  output Nickel,
  output [8:0] TestNumber,
  output Done_Testing
);

  wire not_1_out;

  not not_1 (not_1_out, Halt);
  Counter #(.width(9), .max('h162), .ongoal("stay")) counter_1 (
    .count(not_1_out), .Q(TestNumber), .carry(Done_Testing), .clk(CLK));  // open: load, D, clr
  ROM #(.addrWidth(9), .dataWidth(3)) rom_1 (.addr(TestNumber), .data({Quarter, Dime, Nickel}));  // open: sel

  // Notes on the sheet:
  //   contents of rom_1 (hex, n*v repeats v):
  //   1 0 1 0 1 0 1 0 1 0 1 0 1 0 1 0 1 0 1 0 1 0 2 0 1 0 1 0 1 0 1 0 1 0 4 0 1 0 1 0 1 0 1 0 2 0 1 0 1 0
  //   1 0 1 0 4 0 1 0 1 0 1 0 1 0 2 0 1 0 1 0 1 0 2 0 2 0 1 0 1 0 1 0 2 0 4 0 1 0 1 0 1 0 4 0 1 0 1 0 1 0
  //   1 0 2 0 1 0 1 0 1 0 2 0 2 0 1 0 1 0 1 0 2 0 4 0 1 0 1 0 2 0 2 0 1 0 1 0 2 0 4 0 1 0 1 0 4 0 1 0 1 0
  //   1 0 1 0 2 0 1 0 1 0 1 0 2 0 2 0 1 0 1 0 1 0 2 0 4 0 1 0 1 0 2 0 2 0 1 0 1 0 2 0 4 0 1 0 1 0 2 0 2 0
  //   1 0 2 0 2 0 2 0 1 0 2 0 2 0 4 0 1 0 2 0 4 0 1 0 4 0 1 0 1 0 1 0 1 0 2 0 1 0 1 0 1 0 2 0 2 0 1 0 1 0
  //   1 0 2 0 4 0 1 0 1 0 2 0 2 0 1 0 1 0 2 0 4 0 1 0 1 0 2 0 2 0 1 0 2 0 2 0 2 0 1 0 2 0 2 0 4 0 1 0 2 0
  //   4 0 1 0 1 0 2 0 2 0 1 0 2 0 2 0 2 0 1 0 2 0 2 0 4 0 2 0 2 0 2 0 2 0 2 0 4 0 2 0 4 0 1 0 4 0 2 0 4 0
  //   4 0 4
endmodule

module Checker (
  input  Give_Merch,
  input  Give_Dime,
  input  Give_Nickel,
  input  [8:0] TestNumber,
  output Correct,
  output Sol_Give_Merch,
  output Sol_Give_Dime,
  output Sol_Give_Nickel
);

  ROM #(.addrWidth(9), .dataWidth(3)) rom_1 (
    .addr(TestNumber), .data({Sol_Give_Merch, Sol_Give_Dime, Sol_Give_Nickel}));  // open: sel
  Comparator #(.width(3)) comparator_1 (
    .a({Sol_Give_Merch, Sol_Give_Dime, Sol_Give_Nickel}), .b({Give_Merch, Give_Dime, Give_Nickel}),
    .eq(Correct));  // open: gt, lt

  // Other names for the same wires on the sheet: Solution[2:0] = {Sol_Give_Merch, Sol_Give_Dime, Sol_Give_Nickel};
  //   Your_Answer[2:0] = {Give_Merch, Give_Dime, Give_Nickel}

  // Notes on the sheet:
  //   contents of rom_1 (hex, n*v repeats v):
  //   10*0 4 11*0 5 11*0 7 9*0 4 9*0 7 9*0 4 9*0 5 9*0 7 7*0 6 9*0 4 9*0 5 9*0 7 7*0 4 7*0 7 5*0 5 9*0 4
  //   9*0 5 9*0 7 7*0 4 7*0 7 7*0 4 7*0 5 7*0 7 5*0 6 0 0 0 4 9*0 4 9*0 5 9*0 7 7*0 4 7*0 7 7*0 4 7*0 5
  //   7*0 7 5*0 6 7*0 4 7*0 5 7*0 7 5*0 4 5*0 7 0 0 0 5 0 0 0 4 0 0 0 5 0 0 0 7
endmodule

module NextState (
  input  S2,
  input  S1,
  input  S0,
  input  Quarter,
  input  Dime,
  input  Nickel,
  output S2P,
  output S1P,
  output S0P
);

  wire and_1_out, and_2_out, and_3_out, and_4_out, and_5_out, and_6_out, and_7_out, and_8_out, and_9_out,
       and_10_out, and_11_out, and_12_out, and_13_out, and_14_out, and_15_out, not_1_out, not_2_out,
       not_3_out, not_4_out, not_5_out, not_6_out, not_7_out, not_8_out, not_9_out, not_10_out, not_11_out,
       not_12_out, not_13_out, not_14_out, not_15_out, not_16_out, not_17_out, not_18_out, not_19_out,
       not_20_out, not_21_out, not_22_out, not_23_out, not_24_out, not_25_out, not_26_out, not_27_out,
       not_28_out, not_29_out, not_30_out, not_31_out, not_32_out, not_33_out, not_34_out, not_35_out,
       not_36_out, not_37_out, not_38_out, not_39_out, not_40_out, not_41_out;

  not not_1 (not_1_out, S2);
  not not_2 (not_2_out, Quarter);
  not not_3 (not_3_out, S2);
  not not_4 (not_4_out, S0);
  not not_5 (not_5_out, Dime);
  not not_6 (not_6_out, Nickel);
  not not_7 (not_7_out, S2);
  not not_8 (not_8_out, Quarter);
  not not_9 (not_9_out, S2);
  not not_10 (not_10_out, Quarter);
  not not_11 (not_11_out, Quarter);
  not not_12 (not_12_out, Dime);
  not not_13 (not_13_out, Nickel);
  not not_14 (not_14_out, Quarter);
  not not_15 (not_15_out, Dime);
  not not_16 (not_16_out, Quarter);
  not not_17 (not_17_out, Nickel);
  not not_18 (not_18_out, S2);
  not not_19 (not_19_out, S1);
  not not_20 (not_20_out, Quarter);
  not not_21 (not_21_out, Nickel);
  not not_22 (not_22_out, S2);
  not not_23 (not_23_out, S0);
  not not_24 (not_24_out, Quarter);
  not not_25 (not_25_out, S2);
  not not_26 (not_26_out, Quarter);
  not not_27 (not_27_out, Dime);
  not not_28 (not_28_out, Quarter);
  not not_29 (not_29_out, Dime);
  not not_30 (not_30_out, Nickel);
  not not_31 (not_31_out, S2);
  not not_32 (not_32_out, S1);
  not not_33 (not_33_out, Quarter);
  not not_34 (not_34_out, S2);
  not not_35 (not_35_out, Quarter);
  not not_36 (not_36_out, Nickel);
  not not_37 (not_37_out, Quarter);
  not not_38 (not_38_out, Dime);
  not not_39 (not_39_out, Nickel);
  not not_40 (not_40_out, Quarter);
  not not_41 (not_41_out, Dime);
  and and_1 (and_1_out, not_1_out, not_2_out, Dime, Nickel);
  and and_2 (and_2_out, not_3_out, not_4_out, Quarter, not_5_out, not_6_out);
  and and_3 (and_3_out, not_7_out, S0, not_8_out, Dime);
  and and_4 (and_4_out, not_9_out, S1, not_10_out, Nickel);
  and and_5 (and_5_out, S2, not_11_out, not_12_out, not_13_out);
  and and_6 (and_6_out, S2, S0, not_14_out, not_15_out);
  and and_7 (and_7_out, S2, S1, not_16_out, not_17_out);
  and and_8 (and_8_out, not_18_out, not_19_out, not_20_out, Dime, not_21_out);
  and and_9 (and_9_out, not_22_out, not_23_out, not_24_out, Dime);
  and and_10 (and_10_out, not_25_out, S0, not_26_out, not_27_out, Nickel);
  and and_11 (and_11_out, S1, not_28_out, not_29_out, not_30_out);
  and and_12 (and_12_out, not_31_out, not_32_out, not_33_out, Nickel);
  and and_13 (and_13_out, not_34_out, not_35_out, Dime, not_36_out);
  and and_14 (and_14_out, S0, not_37_out, not_38_out, not_39_out);
  and and_15 (and_15_out, S1, not_40_out, not_41_out);
  or or_1 (S2P, and_1_out, and_2_out, and_3_out, and_4_out, and_5_out, and_6_out, and_7_out);
  or or_2 (S1P, and_8_out, and_9_out, and_10_out, and_11_out);
  or or_3 (S0P, and_12_out, and_13_out, and_14_out, and_15_out);
endmodule

module Output (
  input  S2,
  input  S1,
  input  S0,
  input  Quarter,
  input  Dime,
  input  Nickel,
  output Give_Merchandise,
  output Give_Dime,
  output Give_Nickel
);

  wire and_2_out, and_3_out, and_4_out, and_5_out, and_6_out, and_7_out, and_8_out, not_1_out, not_2_out,
       not_3_out, not_4_out, not_5_out;

  not not_1 (not_1_out, S0);
  not not_2 (not_2_out, S1);
  and and_1 (Give_Dime, S2, Quarter);
  not not_3 (not_3_out, S2);
  not not_4 (not_4_out, S0);
  not not_5 (not_5_out, S1);
  and and_2 (and_2_out, S0, Quarter);
  and and_3 (and_3_out, S2, not_1_out, Nickel);
  and and_4 (and_4_out, S2, not_2_out, Dime);
  and and_5 (and_5_out, S2, Quarter);
  and and_6 (and_6_out, not_3_out, S1, Quarter);
  and and_7 (and_7_out, S2, not_4_out, Dime);
  and and_8 (and_8_out, S2, not_5_out, Quarter);
  or or_1 (Give_Merchandise, and_2_out, and_3_out, and_4_out, and_5_out);
  or or_2 (Give_Nickel, and_6_out, and_7_out, and_8_out);
endmodule
