// Logisim project Divider5.circ as structural Verilog: 7 circuits, main circuit main
module main (
  input  Enable_Halt
);

  wire and_4_out, CLK, Correct, Done_Testing, Halt, Max_Clocks_carry, not_1_out, not_2_out, not_3_out,
       not_4_out, not_5_out, or_1_out, Quotient_Is_Correct, Ready, Remainder_Is_Correct;
  wire [4:0] and_2_out, and_3_out, Correct_Quotient, Correct_Remainder, Dividend, Divisor, Quotient, Ready5,
       Remainder;
  wire [9:0] Test_Number, Tests_Correct_q;

  not not_1 (not_1_out, Correct);
  Counter #(.width(3), .max('h5)) Max_Clocks (
    .load(Ready), .D(3'b000), .count(not_2_out), .carry(Max_Clocks_carry), .clk(CLK));  // open: Q, clr
  not not_2 (not_2_out, Ready);
  Clock clock_1 (.out(CLK));
  and and_1 (Halt, Enable_Halt, Ready, not_1_out);
  or or_1 (or_1_out, Ready, Max_Clocks_carry);
  Inputs inputs_1 (
    .Halt(Halt), .Ready(or_1_out), .CLK(CLK), .Dividend(Dividend), .Divisor(Divisor),
    .TestNumber(Test_Number), .Done(Done_Testing));
  // Probe on Dividend
  // Probe on Divisor
  // Probe on Quotient
  // Probe on Remainder
  // Probe on Correct
  // Probe on Quotient_Is_Correct
  // Probe on Remainder_Is_Correct
  // Probe on Correct_Quotient
  // Probe on Correct_Remainder
  assign and_2_out = Ready5 & Dividend;  // AND_Gate and_2, 5 bits wide
  not not_3 (not_3_out, Halt);
  assign and_3_out = Ready5 & Divisor;  // AND_Gate and_3, 5 bits wide
  not not_4 (not_4_out, Halt);
  not not_5 (not_5_out, Done_Testing);
  Divider5 divider5_1 (
    .Divide(not_3_out), .Dividend(and_2_out), .Divisor(and_3_out), .CLK(CLK), .Ready(Ready),
    .Quotient(Quotient), .Remainder(Remainder));
  and and_4 (and_4_out, Correct, Ready, not_4_out, not_5_out);
  assign Ready5 = {{4{Ready}}, Ready};  // Bit_Extender bit_extender_1
  Counter #(.width(10), .max('h3e1), .ongoal("stay")) Tests_Correct (
    .count(and_4_out), .Q(Tests_Correct_q), .clk(CLK));  // open: load, D, carry, clr
  // Probe on Tests_Correct_q
  Checker checker_1 (
    .TestNumber(Test_Number), .Quotient(Quotient), .Remainder(Remainder), .Correct(Correct),
    .Quotient_Is_Correct(Quotient_Is_Correct), .Remainder_Is_Correct(Remainder_Is_Correct),
    .Correct_Quotient(Correct_Quotient), .Correct_Remainder(Correct_Remainder));

  // Notes on the sheet:
  //   Max: 993
endmodule

module Divider5 (
  input  Divide,
  input  [4:0] Dividend,
  input  [4:0] Divisor,
  input  CLK,
  output Ready,
  output [4:0] Quotient,
  output [4:0] Remainder
);

  wire comparator_1_eq, comparator_1_gt, Curr_Bit_Div, Dividing, or_3_out, or_4_out, RemGTDivr, Start;
  wire [2:0] Index;
  wire [4:0] bit_extender_1_out, CheckRem, Divd, Divr, multiplexer_1_out, multiplexer_2_out,
       multiplexer_3_out, multiplexer_4_out, or_2_out, shifter_1_out, shifter_2_out, subtractor_1_out,
       subtractor_2_out;

  assign bit_extender_1_out = {{4{1'b0}}, Curr_Bit_Div};  // Bit_Extender bit_extender_1
  Shifter #(.width(5)) shifter_1 (.in(Remainder), .\dist (3'b001), .out(shifter_1_out));
  Subtractor #(.width(5)) subtractor_1 (.a(shifter_1_out), .b(Divr), .out(subtractor_1_out));  // open: bin, bout
  assign CheckRem = shifter_1_out | bit_extender_1_out;  // OR_Gate or_1, 5 bits wide
  Subtractor #(.width(5)) subtractor_2 (.a(CheckRem), .b(Divr), .out(subtractor_2_out));  // open: bin, bout
  assign or_2_out = shifter_2_out | 5'b00001;  // OR_Gate or_2, 5 bits wide
  Multiplexer #(.select(2), .width(5), .enable("false")) multiplexer_1 (
    .in0(shifter_1_out), .in1(subtractor_1_out), .in2(CheckRem), .in3(subtractor_2_out),
    .out(multiplexer_1_out), .sel({Curr_Bit_Div, RemGTDivr}));
  Shifter #(.width(5)) shifter_2 (.in(Quotient), .\dist (3'b001), .out(shifter_2_out));
  // Probe on Divd
  Register #(.width(5)) u_dividend (.D(Dividend), .en(Start), .Q(Divd), .clk(CLK));  // open: clr
  Register #(.width(5)) u_divisor (.D(Divisor), .en(Start), .Q(Divr), .clk(CLK));  // open: clr
  Multiplexer #(.width(5), .enable("false")) multiplexer_2 (
    .in0(shifter_2_out), .in1(or_2_out), .out(multiplexer_2_out), .sel(RemGTDivr));
  Multiplexer #(.width(5), .enable("false")) multiplexer_3 (
    .in0({5{1'b0}}), .in1(multiplexer_1_out), .out(multiplexer_3_out), .sel(Dividing));
  or or_3 (or_3_out, Start, Dividing);
  Comparator #(.width(5), .mode("unsigned")) comparator_1 (
    .a(CheckRem), .b(Divr), .gt(comparator_1_gt), .eq(comparator_1_eq));  // open: lt
  // Probe on Divr
  Multiplexer #(.width(5), .enable("false")) multiplexer_4 (
    .in0({5{1'b0}}), .in1(multiplexer_2_out), .out(multiplexer_4_out), .sel(Dividing));
  or or_4 (or_4_out, Start, Dividing);
  // Probe on Remainder
  Register #(.width(5)) u_remainder (.D(multiplexer_3_out), .en(or_3_out), .Q(Remainder), .clk(CLK));  // open: clr
  or or_5 (RemGTDivr, comparator_1_gt, comparator_1_eq);
  // Probe on Quotient
  Register #(.width(5)) u_quotient (.D(multiplexer_4_out), .en(or_4_out), .Q(Quotient), .clk(CLK));  // open: clr
  controller controller (
    .Divide(Divide), .CLK(CLK), .Start(Start), .Dividing(Dividing), .I2(Index[2]), .I1(Index[1]),
    .I0(Index[0]), .Ready(Ready));
  // Probe on Curr_Bit_Div
  Multiplexer #(.select(3), .enable("false")) multiplexer_5 (
    .in0(Divd[0]), .in1(Divd[1]), .in2(Divd[2]), .in3(Divd[3]), .in4(Divd[4]), .in5(1'b0), .in6(1'b0),
    .in7(1'b0), .out(Curr_Bit_Div), .sel(Index));
  // Probe on Index
endmodule

module Inputs (
  input  Halt,
  input  Ready,
  input  CLK,
  output [4:0] Dividend,
  output [4:0] Divisor,
  output [9:0] TestNumber,
  output Done
);

  wire and_1_out, not_1_out;

  not not_1 (not_1_out, Halt);
  and and_1 (and_1_out, not_1_out, Ready);
  Counter #(.width(10), .max('h3e1), .ongoal("stay")) u_TestNumber (
    .count(and_1_out), .Q(TestNumber), .carry(Done), .clk(CLK));  // open: load, D, clr
  ROM #(.addrWidth(10), .dataWidth(10)) rom_1 (.addr(TestNumber), .data({Dividend, Divisor}));  // open: sel

  // Notes on the sheet:
  //   contents of rom_1 (hex, n*v repeats v):
  //   1 2 3 4 5 6 7 8 9 a b c d e f 10 11 12 13 14 15 16 17 18 19 1a 1b 1c 1d 1e 1f 21 22 23 24 25 26 27
  //   28 29 2a 2b 2c 2d 2e 2f 30 31 32 33 34 35 36 37 38 39 3a 3b 3c 3d 3e 3f 41 42 43 44 45 46 47 48 49
  //   4a 4b 4c 4d 4e 4f 50 51 52 53 54 55 56 57 58 59 5a 5b 5c 5d 5e 5f 61 62 63 64 65 66 67 68 69 6a 6b
  //   6c 6d 6e 6f 70 71 72 73 74 75 76 77 78 79 7a 7b 7c 7d 7e 7f 81 82 83 84 85 86 87 88 89 8a 8b 8c 8d
  //   8e 8f 90 91 92 93 94 95 96 97 98 99 9a 9b 9c 9d 9e 9f a1 a2 a3 a4 a5 a6 a7 a8 a9 aa ab ac ad ae af
  //   b0 b1 b2 b3 b4 b5 b6 b7 b8 b9 ba bb bc bd be bf c1 c2 c3 c4 c5 c6 c7 c8 c9 ca cb cc cd ce cf d0 d1
  //   d2 d3 d4 d5 d6 d7 d8 d9 da db dc dd de df e1 e2 e3 e4 e5 e6 e7 e8 e9 ea eb ec ed ee ef f0 f1 f2 f3
  //   f4 f5 f6 f7 f8 f9 fa fb fc fd fe ff 101 102 103 104 105 106 107 108 109 10a 10b 10c 10d 10e 10f 110
  //   111 112 113 114 115 116 117 118 119 11a 11b 11c 11d 11e 11f 121 122 123 124 125 126 127 128 129 12a
  //   12b 12c 12d 12e 12f 130 131 132 133 134 135 136 137 138 139 13a 13b 13c 13d 13e 13f 141 142 143 144
  //   145 146 147 148 149 14a 14b 14c 14d 14e 14f 150 151 152 153 154 155 156 157 158 159 15a 15b 15c 15d
  //   15e 15f 161 162 163 164 165 166 167 168 169 16a 16b 16c 16d 16e 16f 170 171 172 173 174 175 176 177
  //   178 179 17a 17b 17c 17d 17e 17f 181 182 183 184 185 186 187 188 189 18a 18b 18c 18d 18e 18f 190 191
  //   192 193 194 195 196 197 198 199 19a 19b 19c 19d 19e 19f 1a1 1a2 1a3 1a4 1a5 1a6 1a7 1a8 1a9 1aa 1ab
  //   1ac 1ad 1ae 1af 1b0 1b1 1b2 1b3 1b4 1b5 1b6 1b7 1b8 1b9 1ba 1bb 1bc 1bd 1be 1bf 1c1 1c2 1c3 1c4 1c5
  //   1c6 1c7 1c8 1c9 1ca 1cb 1cc 1cd 1ce 1cf 1d0 1d1 1d2 1d3 1d4 1d5 1d6 1d7 1d8 1d9 1da 1db 1dc 1dd 1de
  //   1df 1e1 1e2 1e3 1e4 1e5 1e6 1e7 1e8 1e9 1ea 1eb 1ec 1ed 1ee 1ef 1f0 1f1 1f2 1f3 1f4 1f5 1f6 1f7 1f8
  //   1f9 1fa 1fb 1fc 1fd 1fe 1ff 201 202 203 204 205 206 207 208 209 20a 20b 20c 20d 20e 20f 210 211 212
  //   213 214 215 216 217 218 219 21a 21b 21c 21d 21e 21f 221 222 223 224 225 226 227 228 229 22a 22b 22c
  //   22d 22e 22f 230 231 232 233 234 235 236 237 238 239 23a 23b 23c 23d 23e 23f 241 242 243 244 245 246
  //   247 248 249 24a 24b 24c 24d 24e 24f 250 251 252 253 254 255 256 257 258 259 25a 25b 25c 25d 25e 25f
  //   261 262 263 264 265 266 267 268 269 26a 26b 26c 26d 26e 26f 270 271 272 273 274 275 276 277 278 279
  //   27a 27b 27c 27d 27e 27f 281 282 283 284 285 286 287 288 289 28a 28b 28c 28d 28e 28f 290 291 292 293
  //   294 295 296 297 298 299 29a 29b 29c 29d 29e 29f 2a1 2a2 2a3 2a4 2a5 2a6 2a7 2a8 2a9 2aa 2ab 2ac 2ad
  //   2ae 2af 2b0 2b1 2b2 2b3 2b4 2b5 2b6 2b7 2b8 2b9 2ba 2bb 2bc 2bd 2be 2bf 2c1 2c2 2c3 2c4 2c5 2c6 2c7
  //   2c8 2c9 2ca 2cb 2cc 2cd 2ce 2cf 2d0 2d1 2d2 2d3 2d4 2d5 2d6 2d7 2d8 2d9 2da 2db 2dc 2dd 2de 2df 2e1
  //   2e2 2e3 2e4 2e5 2e6 2e7 2e8 2e9 2ea 2eb 2ec 2ed 2ee 2ef 2f0 2f1 2f2 2f3 2f4 2f5 2f6 2f7 2f8 2f9 2fa
  //   2fb 2fc 2fd 2fe 2ff 301 302 303 304 305 306 307 308 309 30a 30b 30c 30d 30e 30f 310 311 312 313 314
  //   315 316 317 318 319 31a 31b 31c 31d 31e 31f 321 322 323 324 325 326 327 328 329 32a 32b 32c 32d 32e
  //   32f 330 331 332 333 334 335 336 337 338 339 33a 33b 33c 33d 33e 33f 341 342 343 344 345 346 347 348
  //   349 34a 34b 34c 34d 34e 34f 350 351 352 353 354 355 356 357 358 359 35a 35b 35c 35d 35e 35f 361 362
  //   363 364 365 366 367 368 369 36a 36b 36c 36d 36e 36f 370 371 372 373 374 375 376 377 378 379 37a 37b
  //   37c 37d 37e 37f 381 382 383 384 385 386 387 388 389 38a 38b 38c 38d 38e 38f 390 391 392 393 394 395
  //   396 397 398 399 39a 39b 39c 39d 39e 39f 3a1 3a2 3a3 3a4 3a5 3a6 3a7 3a8 3a9 3aa 3ab 3ac 3ad 3ae 3af
  //   3b0 3b1 3b2 3b3 3b4 3b5 3b6 3b7 3b8 3b9 3ba 3bb 3bc 3bd 3be 3bf 3c1 3c2 3c3 3c4 3c5 3c6 3c7 3c8 3c9
  //   3ca 3cb 3cc 3cd 3ce 3cf 3d0 3d1 3d2 3d3 3d4 3d5 3d6 3d7 3d8 3d9 3da 3db 3dc 3dd 3de 3df 3e1 3e2 3e3
  //   3e4 3e5 3e6 3e7 3e8 3e9 3ea 3eb 3ec 3ed 3ee 3ef 3f0 3f1 3f2 3f3 3f4 3f5 3f6 3f7 3f8 3f9 3fa 3fb 3fc
  //   3fd 3fe 3ff
endmodule

module Checker (
  input  [9:0] TestNumber,
  input  [4:0] Quotient,
  input  [4:0] Remainder,
  output Correct,
  output Quotient_Is_Correct,
  output Remainder_Is_Correct,
  output [4:0] Correct_Quotient,
  output [4:0] Correct_Remainder
);

  ROM #(.addrWidth(10), .dataWidth(10)) rom_1 (
    .addr(TestNumber), .data({Correct_Quotient, Correct_Remainder}));  // open: sel
  Comparator #(.width(5), .mode("unsigned")) comparator_1 (
    .a(Quotient), .b(Correct_Quotient), .eq(Quotient_Is_Correct));  // open: gt, lt
  Comparator #(.width(5), .mode("unsigned")) comparator_2 (
    .a(Remainder), .b(Correct_Remainder), .eq(Remainder_Is_Correct));  // open: gt, lt
  and and_1 (Correct, Quotient_Is_Correct, Remainder_Is_Correct);

  // Notes on the sheet:
  //   contents of rom_1 (hex, n*v repeats v):
  //   32*0 20 30*1 40 20 29*2 60 21 20 28*3 80 40 21 20 27*4 a0 41 22 21 20 26*5 c0 60 40 22 21 20 25*6 e0
  //   61 41 23 22 21 20 24*7 100 80 42 40 23 22 21 20 23*8 120 81 60 41 24 23 22 21 20 22*9 140 a0 61 42
  //   40 24 23 22 21 20 21*a 160 a1 62 43 41 25 24 23 22 21 20 20*b 180 c0 80 60 42 40 25 24 23 22 21 20
  //   19*c 1a0 c1 81 61 43 41 26 25 24 23 22 21 20 18*d 1c0 e0 82 62 44 42 40 26 25 24 23 22 21 20 17*e
  //   1e0 e1 a0 63 60 43 41 27 26 25 24 23 22 21 20 16*f 200 100 a1 80 61 44 42 40 27 26 25 24 23 22 21 20
  //   15*10 220 101 a2 81 62 45 43 41 28 27 26 25 24 23 22 21 20 14*11 240 120 c0 82 63 60 44 42 40 28 27
  //   26 25 24 23 22 21 20 13*12 260 121 c1 83 64 61 45 43 41 29 28 27 26 25 24 23 22 21 20 12*13 280 140
  //   c2 a0 80 62 46 44 42 40 29 28 27 26 25 24 23 22 21 20 11*14 2a0 141 e0 a1 81 63 60 45 43 41 2a 29 28
  //   27 26 25 24 23 22 21 20 10*15 2c0 160 e1 a2 82 64 61 46 44 42 40 2a 29 28 27 26 25 24 23 22 21 20
  //   9*16 2e0 161 e2 a3 83 65 62 47 45 43 41 2b 2a 29 28 27 26 25 24 23 22 21 20 8*17 300 180 100 c0 84
  //   80 63 60 46 44 42 40 2b 2a 29 28 27 26 25 24 23 22 21 20 7*18 320 181 101 c1 a0 81 64 61 47 45 43 41
  //   2c 2b 2a 29 28 27 26 25 24 23 22 21 20 6*19 340 1a0 102 c2 a1 82 65 62 48 46 44 42 40 2c 2b 2a 29 28
  //   27 26 25 24 23 22 21 20 5*1a 360 1a1 120 c3 a2 83 66 63 60 47 45 43 41 2d 2c 2b 2a 29 28 27 26 25 24
  //   23 22 21 20 4*1b 380 1c0 121 e0 a3 84 80 64 61 48 46 44 42 40 2d 2c 2b 2a 29 28 27 26 25 24 23 22 21
  //   20 1c 1c 1c 3a0 1c1 122 e1 a4 85 81 65 62 49 47 45 43 41 2e 2d 2c 2b 2a 29 28 27 26 25 24 23 22 21
  //   20 1d 1d 3c0 1e0 140 e2 c0 a0 82 66 63 60 48 46 44 42 40 2e 2d 2c 2b 2a 29 28 27 26 25 24 23 22 21
  //   20 1e 3e0 1e1 141 e3 c1 a1 83 67 64 61 49 47 45 43 41 2f 2e 2d 2c 2b 2a 29 28 27 26 25 24 23 22 21
  //   20
endmodule

module controller (
  input  Divide,
  input  CLK,
  output Start,
  output Dividing,
  output I2,
  output I1,
  output I0,
  output Ready
);

  wire S0, S0P, S1, S1P, S2, S2P;

  nextState nextstate_1 (.S2(S2), .S1(S1), .S0(S0), .Divide(Divide), .S2P(S2P), .S1P(S1P), .S0P(S0P));
  Register #(.width(3)) register_1 (.D({S2P, S1P, S0P}), .Q({S2, S1, S0}), .clk(CLK));  // open: en, clr
  \output  output_1 (
    .S2(S2), .S1(S1), .S0(S0), .Divide(Divide), .Start(Start), .Dividing(Dividing), .I2(I2), .I1(I1),
    .I0(I0), .Ready(Ready));
endmodule

module nextState (
  input  S2,
  input  S1,
  input  S0,
  input  Divide,
  output S2P,
  output S1P,
  output S0P
);

  wire and_2_out, and_3_out, and_4_out, not_1_out, not_2_out, not_3_out;

  and and_1 (S2P, S1, not_1_out);
  not not_1 (not_1_out, S0);
  not not_2 (not_2_out, S0);
  and and_2 (and_2_out, not_2_out, Divide);
  and and_3 (and_3_out, S1, not_3_out);
  not not_3 (not_3_out, S0);
  and and_4 (and_4_out, S1, S0);
  or or_1 (S1P, and_2_out, and_3_out, S2);
  or or_2 (S0P, and_4_out, S2);
endmodule

module \output  (
  input  S2,
  input  S1,
  input  S0,
  input  Divide,
  output Start,
  output Dividing,
  output I2,
  output I1,
  output I0,
  output Ready
);

  wire and_1_out, and_2_out, and_4_out, and_5_out, not_1_out, not_2_out, not_3_out, not_4_out, not_5_out,
       not_6_out, not_7_out, not_8_out, not_9_out, not_10_out;

  not not_1 (not_1_out, S1);
  and and_1 (and_1_out, not_1_out, not_2_out, Divide);
  not not_2 (not_2_out, S0);
  and and_2 (and_2_out, S2, not_3_out);
  not not_3 (not_3_out, S1);
  or or_1 (Dividing, S0, S1);
  not not_4 (not_4_out, S2);
  and and_3 (I2, not_4_out, not_5_out);
  not not_5 (not_5_out, S0);
  not not_6 (not_6_out, S2);
  and and_4 (and_4_out, not_6_out, S1, S0);
  and and_5 (and_5_out, S2, not_7_out);
  not not_7 (not_7_out, S0);
  not not_8 (not_8_out, S2);
  and and_6 (Ready, not_8_out, not_9_out, not_10_out);
  not not_9 (not_9_out, S1);
  not not_10 (not_10_out, S0);
  or or_2 (Start, and_1_out, and_2_out);
  or or_3 (I0, and_4_out, and_5_out);

  assign I1 = S2;
endmodule
